# Fritzing sketch Servo Motor (saved by Fritzing 0.8.7b)
breadboards: 1

parts:
  Part1 = Arduino Uno (Rev3)
  J1 = Basic Servo

nets:
  N1: Part1.D3_PWM, J1.pulse
  5V: Part1.5V, J1.vcc
  GND: Part1.GND, J1.gnd

notes:
  Designed by NDABAHARIYE Jea Aime - 0785384384
  Email: aimegenie@gmail.com
